// Logisim project CPU_8085.circ as structural Verilog: 11 circuits, main circuit main
module main (
  input  [4:0] Select_instruction,
  input  Cin,
  input  [15:0] AC,
  input  [15:0] DR,
  output C_out,
  output [15:0] ALU_out
);

  wire add_sub_1_sign, add_sub_1_zero, clock_1_out, cO, flag_1_flagout, multiplexer_1_out, multiplexer_2_out,
       register_1_q;
  wire [1:0] multiplexer_3_out, multiplexer_4_out;
  wire [15:0] add_sub_1_o, logical_1_logical_out, multiplexer_5_out;
  wire [15:15] not_1_out;

  Multiplexer multiplexer_1 (
    .in0(Select_instruction[2]), .in1(1'b0), .out(multiplexer_1_out), .sel(Select_instruction[4]));
  Register #(.width(1)) register_1 (.D(cO), .en(1'b1), .Q(register_1_q));  // open: clk, clr
  Multiplexer multiplexer_2 (.in0(Cin), .in1(1'b1), .out(multiplexer_2_out), .sel(Select_instruction[4]));
  Multiplexer #(.width(2)) multiplexer_3 (
    .in0(Select_instruction[1:0]), .in1(2'b10), .out(multiplexer_3_out), .sel(Select_instruction[4]));
  Clock clock_1 (.out(clock_1_out));
  Multiplexer #(.width(2)) multiplexer_4 (
    .in0(2'b11), .in1(Select_instruction[1:0]), .out(multiplexer_4_out), .sel(Select_instruction[4]));
  flag flag_1 (
    .zero(add_sub_1_zero), .sign(add_sub_1_sign), .carry(register_1_q), .selflag(multiplexer_4_out),
    .flagout(flag_1_flagout));
  add_sub add_sub_1 (
    .A(AC), .cin(multiplexer_2_out), .B(DR), .s(multiplexer_3_out), .clock(clock_1_out),
    .selecn(multiplexer_1_out), .o(add_sub_1_o), .Carry(C_out), .sign(add_sub_1_sign), .zero(add_sub_1_zero));
  not not_1 (not_1_out[15], flag_1_flagout);
  logical logical_1 (
    .cI(not_1_out[15]), .AC(AC), .DR(DR), .selectL(Select_instruction[2:0]), .cO(cO),
    .Logical_out(logical_1_logical_out));
  Multiplexer #(.width(16)) multiplexer_5 (
    .in0(add_sub_1_o), .in1(logical_1_logical_out), .out(multiplexer_5_out), .sel(Select_instruction[3]));
  Multiplexer #(.width(16)) multiplexer_6 (
    .in0(multiplexer_5_out), .in1({16{not_1_out[15]}}), .out(ALU_out), .sel(Select_instruction[4]));

  // Other names for the same wires on the sheet: S45[1:0] = Select_instruction[1:0];
  //   S345[2:0] = Select_instruction[2:0]; S3 = Select_instruction[2]; S2 = Select_instruction[3];
  //   S1 = Select_instruction[4]
endmodule

module BIT_16 (
  input  [15:0] loadin,
  input  INR,
  input  CLR,
  input  LOAD,
  input  clk,
  output [15:0] out_6
);

  wire adder_1_cout;
  wire [15:0] adder_1_out, multiplexer_1_out, multiplexer_2_out, multiplexer_3_out;

  LED led_1 (.in(adder_1_cout));
  Adder #(.width(16)) adder_1 (.a(out_6), .b(16'h1), .out(adder_1_out), .cin(1'b0), .cout(adder_1_cout));
  Multiplexer #(.width(16)) multiplexer_1 (.in0(out_6), .in1(adder_1_out), .out(multiplexer_1_out), .sel(INR));
  Multiplexer #(.width(16)) multiplexer_2 (
    .in0(multiplexer_1_out), .in1({16{1'b0}}), .out(multiplexer_2_out), .sel(CLR));
  Multiplexer #(.width(16)) multiplexer_3 (.in0(multiplexer_2_out), .in1(loadin), .out(multiplexer_3_out), .sel(LOAD));
  Register #(.width(16)) register_1 (.D(multiplexer_3_out), .en(1'b1), .clk(clk), .Q(out_6));  // open: clr

  // Notes on the sheet:
  //   AC_16
endmodule

module BIT_12 (
  input  [11:0] loadin,
  input  INR,
  input  CLR,
  input  LOAD,
  input  clk,
  output [11:0] out_6
);

  wire adder_1_cout;
  wire [11:0] adder_1_out, multiplexer_1_out, multiplexer_2_out, multiplexer_3_out;

  Adder #(.width(12)) adder_1 (.a(out_6), .b(12'h1), .out(adder_1_out), .cin(1'b0), .cout(adder_1_cout));
  LED led_1 (.in(adder_1_cout));
  Multiplexer #(.width(12)) multiplexer_1 (.in0(out_6), .in1(adder_1_out), .out(multiplexer_1_out), .sel(INR));
  Multiplexer #(.width(12)) multiplexer_2 (
    .in0(multiplexer_1_out), .in1({12{1'b0}}), .out(multiplexer_2_out), .sel(CLR));
  Multiplexer #(.width(12)) multiplexer_3 (.in0(multiplexer_2_out), .in1(loadin), .out(multiplexer_3_out), .sel(LOAD));
  Register #(.width(12)) register_1 (.D(multiplexer_3_out), .en(1'b1), .clk(clk), .Q(out_6));  // open: clr

  // Notes on the sheet:
  //   12 BIT
endmodule

module DATA_PATH_UNIT (
  input  [15:0] in_1,
  input  Start,
  output [11:0] out_3,
  output [11:0] out_4,
  output [15:0] DR_out,
  output [15:0] AC_out,
  output [15:0] IR_OUT,
  output [15:0] TR_OUT,
  output [4:0] out_9
);

  wire CLK, CLR_AC, CLR_AR, CLR_DR, CLR_PC, CLR_TR, INR_AC, INR_AR, INR_DR, INR_PC, INR_TR, IR_LDR, LOAD_AC,
       LOAD_ALU, LOAD_AR, LOAD_DR, LOAD_PC, LOAD_TR, main_1_c_out, OUTPUT_en, register_1_q, Write_en;
  wire [2:0] SELECT_OUT;
  wire [15:0] ALU_out, multiplexer_1_out, or_1_out, ram_1_dout;

  Clock clock_1 (.out(CLK));
  RAM #(.addrWidth(12), .asyncread("true"), .dataWidth(16)) ram_1 (
    .addr(out_3), .we(Write_en), .oe(OUTPUT_en), .clk(CLK),
    .din({{4{multiplexer_1_out[15]}}, multiplexer_1_out[11:0]}), .dout(ram_1_dout));
  BIT_12 AR (.loadin(multiplexer_1_out[11:0]), .INR(INR_AR), .CLR(CLR_AR), .LOAD(LOAD_AR), .clk(CLK), .out_6(out_3));
  BIT_12 PC (.loadin(multiplexer_1_out[11:0]), .INR(INR_PC), .CLR(CLR_PC), .LOAD(LOAD_PC), .clk(CLK), .out_6(out_4));
  BIT_16 DR (
    .loadin({{4{multiplexer_1_out[15]}}, multiplexer_1_out[11:0]}), .INR(INR_DR), .CLR(CLR_DR),
    .LOAD(LOAD_DR), .clk(CLK), .out_6(DR_out));
  AC ac_1 (
    .loadin({{4{multiplexer_1_out[15]}}, multiplexer_1_out[11:0]}), .ALUI_N(ALU_out), .CLK(CLK),
    .LOAD_ALU(LOAD_ALU), .INR(INR_AC), .CLR(CLR_AC), .LOAD(LOAD_AC), .out_8(AC_out));
  IR ir_1 (.loadin({{4{multiplexer_1_out[15]}}, multiplexer_1_out[11:0]}), .Load(IR_LDR), .clk(CLK), .out_4(IR_OUT));
  BIT_16 TR (
    .loadin({{4{multiplexer_1_out[15]}}, multiplexer_1_out[11:0]}), .INR(INR_TR), .CLR(CLR_TR),
    .LOAD(LOAD_TR), .clk(CLK), .out_6(TR_OUT));
  assign or_1_out = DR_out | in_1;  // OR_Gate or_1, 16 bits wide
  Multiplexer #(.select(3), .width(16)) multiplexer_1 (
    .in0({16{1'b0}}), .in1({4'b0000, out_3}), .in2({4'b0000, out_4}), .in3(DR_out), .in4(AC_out),
    .in5(IR_OUT), .in6(TR_OUT), .in7(ram_1_dout),
    .out({{4{multiplexer_1_out[15]}}, multiplexer_1_out[11:0]}), .sel(SELECT_OUT));
  Register #(.width(1)) register_1 (.D(main_1_c_out), .en(1'b1), .Q(register_1_q));  // open: clk, clr
  main main_1 (
    .Select_instruction(IR_OUT[8:4]), .Cin(register_1_q), .AC(AC_out), .DR(or_1_out), .C_out(main_1_c_out),
    .ALU_out(ALU_out));
  Time_sequence time_sequence_1 (
    .CLK(CLK), .Start(Start), .LOAD_AR(LOAD_AR), .CLR_AR(CLR_AR), .INR_AR(INR_AR), .LOAD_PC(LOAD_PC),
    .CLR_PC(CLR_PC), .INR_PC(INR_PC), .LOAD_DR(LOAD_DR), .CLR_DR(CLR_DR), .INR_DR(INR_DR),
    .LOAD_ALU(LOAD_ALU), .LOAD_AC(LOAD_AC), .CLR_AC(CLR_AC), .INR_AC(INR_AC), .IR_LDR(IR_LDR),
    .LOAD_TR(LOAD_TR), .CLR_TR(CLR_TR), .INR_TR(INR_TR), .Write_en(Write_en), .OUTPUT_en(OUTPUT_en),
    .SELECT_OUT(SELECT_OUT));

  assign out_9 = IR_OUT[8:4];
  // also tied to GND on the sheet: multiplexer_1_out[15]

  // Other names for the same wires on the sheet: ACO[15:0] = AC_out; DR[15:0] = DR_out; IR1[15:0] = IR_OUT;
  //   ALU_selecT[4:0] = IR_OUT[8:4]

  // Notes on the sheet:
  //   Data Path Unit Using Multiplexer
  //   AC
  //   IR
endmodule

module add_sub (
  input  [15:0] A,
  input  cin,
  input  [15:0] B,
  input  [1:0] s,
  input  clock,
  input  selecn,
  output [15:0] o,
  output Carry,
  output sign,
  output zero
);

  wire and_1_out, flag_1_flagout, or_1_out, or_2_out;
  wire [15:0] multiplexer_1_out, multiplexer_2_out, not_1_out, register_1_q;

  assign not_1_out = ~B;  // NOT_Gate not_1, 16 bits wide
  flag flag_1 (.zero(sign), .selflag({1'b0, selecn}), .flagout(flag_1_flagout));  // open: sign, carry
  or or_1 (or_1_out, selecn, 1'b0);
  Multiplexer #(.select(2), .width(16)) multiplexer_1 (
    .in0({16{1'b0}}), .in1(B), .in2(not_1_out), .in3({16{1'b1}}), .out(multiplexer_1_out), .sel(s));
  and and_1 (and_1_out, flag_1_flagout, clock);
  Multiplexer #(.width(16)) multiplexer_2 (.in0(A), .in1(register_1_q), .out(multiplexer_2_out), .sel(or_1_out));
  Register #(.width(16)) register_1 (.D(o), .clk(and_1_out), .Q(register_1_q));  // open: en, clr
  Adder #(.width(16)) adder_1 (.a(multiplexer_2_out), .b(multiplexer_1_out), .out(o), .cin(cin), .cout(Carry));
  or or_2 (or_2_out, o[15], o[14], o[13], o[12], o[11], o[10], o[9], o[8], o[6], o[5], o[4], o[3], o[2], o[1], o[7], o[0]);
  not not_2 (sign, or_2_out);

  assign zero = o[15];

  // Other names for the same wires on the sheet: car = Carry; sign_t = o[15]; zero_t = sign
endmodule

module logical (
  input  cI,
  input  [15:0] AC,
  input  [15:0] DR,
  input  [2:0] selectL,
  output cO,
  output [15:0] Logical_out
);

  wire [15:0] and_1_out, not_1_out, or_1_out, xor_1_out;

  Multiplexer #(.select(2)) multiplexer_1 (
    .in0(AC[14]), .in1(AC[0]), .in2(AC[15]), .in3(AC[0]), .out(cO), .sel(selectL[1:0]));
  LED led_1 (.in(cI));
  assign and_1_out = AC & DR;  // AND_Gate and_1, 16 bits wide
  assign or_1_out = AC | DR;  // OR_Gate or_1, 16 bits wide
  assign xor_1_out = AC ^ DR;  // XOR_Gate xor_1, 16 bits wide
  assign not_1_out = ~AC;  // NOT_Gate not_1, 16 bits wide
  Multiplexer #(.select(3), .width(16)) multiplexer_2 (
    .in0(and_1_out), .in1(or_1_out), .in2(xor_1_out), .in3(not_1_out), .in4({AC[14:0], AC[15]}),
    .in5({AC[0], AC[15:1]}), .in6({AC[14:0], cI}), .in7({cI, AC[15:1]}), .out(Logical_out), .sel(selectL));

  // Other names for the same wires on the sheet: SELR[1:0] = selectL[1:0]
endmodule

module flag (
  input  zero,
  input  sign,
  input  carry,
  input  [1:0] selflag,
  output flagout
);

  wire multiplexer_1_out;

  Multiplexer #(.select(2)) multiplexer_1 (
    .in0(1'b0), .in1(zero), .in2(sign), .in3(carry), .out(multiplexer_1_out), .sel(selflag));
  not not_1 (flagout, multiplexer_1_out);
endmodule

module alogic (
  input  [15:0] a,
  input  [15:0] b,
  input  [1:0] s,
  output [15:0] o
);

  wire add_sub_1_carry, add_sub_1_sign, clock_1_out, flag_1_flagout;

  Clock clock_1 (.out(clock_1_out));
  flag flag_1 (.zero(add_sub_1_sign), .sign(add_sub_1_carry), .selflag(s), .flagout(flag_1_flagout));  // open: carry
  not not_1 (o[15], flag_1_flagout);
  add_sub add_sub_1 (
    .A(a), .cin(1'b1), .B(b), .s(2'b10), .clock(clock_1_out), .selecn(1'b0), .Carry(add_sub_1_carry),
    .sign(add_sub_1_sign));  // open: o, zero

  assign o[14:0] = {15{o[15]}};
endmodule

module AC (
  input  [15:0] loadin,
  input  [15:0] ALUI_N,
  input  CLK,
  input  LOAD_ALU,
  input  INR,
  input  CLR,
  input  LOAD,
  output [15:0] out_8
);

  wire [15:0] adder_1_out, multiplexer_1_out, multiplexer_2_out, multiplexer_3_out, multiplexer_4_out;

  Adder #(.width(16)) adder_1 (.a(out_8), .b(16'h1), .out(adder_1_out), .cin(1'b0));  // open: cout
  Multiplexer #(.width(16)) multiplexer_1 (.in0(out_8), .in1(adder_1_out), .out(multiplexer_1_out), .sel(INR));
  Multiplexer #(.width(16)) multiplexer_2 (
    .in0(multiplexer_1_out), .in1({16{1'b0}}), .out(multiplexer_2_out), .sel(CLR));
  Multiplexer #(.width(16)) multiplexer_3 (.in0(multiplexer_2_out), .in1(loadin), .out(multiplexer_3_out), .sel(LOAD));
  Multiplexer #(.width(16)) multiplexer_4 (
    .in0(multiplexer_3_out), .in1(ALUI_N), .out(multiplexer_4_out), .sel(LOAD_ALU));
  Register #(.width(16)) register_1 (.D(multiplexer_4_out), .en(1'b1), .clk(CLK), .Q(out_8));  // open: clr
endmodule

module IR (
  input  [15:0] loadin,
  input  Load,
  input  clk,
  output [15:0] out_4
);

  wire I;
  wire [4:0] register_1_q;
  wire [15:0] multiplexer_1_out;

  Multiplexer #(.width(16)) multiplexer_1 (
    .in0({I, register_1_q, out_4[9:0]}), .in1(loadin), .out(multiplexer_1_out), .sel(Load));
  Register #(.width(16)) register_1 (
    .D(multiplexer_1_out), .en(1'b1), .clk(clk), .Q({I, register_1_q, out_4[9:0]}));  // open: clr

  assign out_4[15:10] = {6{1'b0}};

  // Notes on the sheet:
  //   LOAD
  //   AC_16
endmodule

module Time_sequence (
  input  CLK,
  input  Start,
  output LOAD_AR,
  output CLR_AR,
  output INR_AR,
  output LOAD_PC,
  output CLR_PC,
  output INR_PC,
  output LOAD_DR,
  output CLR_DR,
  output INR_DR,
  output LOAD_ALU,
  output LOAD_AC,
  output CLR_AC,
  output INR_AC,
  output IR_LDR,
  output LOAD_TR,
  output CLR_TR,
  output INR_TR,
  output Write_en,
  output OUTPUT_en,
  output [2:0] SELECT_OUT
);

  wire T0, T1, T2, T3, T4, T5, T6, T7, T8, T9, T10, T11, T12, T13, T14, T15, X1, X2, X3, X4, X5, X6, X7, X8;
  wire [3:0] adder_1_out, register_1_q;

  Adder #(.width(4)) adder_1 (.a(register_1_q), .b({3'b000, CLK}), .out(adder_1_out));  // open: cin, cout
  Register #(.trigger("falling"), .width(4)) register_1 (
    .D(adder_1_out), .clk(CLK), .Q(register_1_q), .clr(Start));  // open: en
  or or_1 (INR_AR, 1'b0, 1'b0);
  or or_2 (CLR_PC, Start, 1'b0);
  buf or_3 (LOAD_DR, 1'b0);  // OR_Gate
  or or_4 (INR_DR, 1'b0, 1'b0);
  or or_5 (LOAD_AC, T4, T10, 1'b0);
  or or_6 (INR_AC, T8, 1'b0);
  or or_7 (LOAD_TR, T12, 1'b0);
  or or_8 (INR_TR, 1'b0, 1'b0);
  or or_9 (OUTPUT_en, T2, T6, 1'b0, T9, T4, T11);
  or or_10 (X2, 1'b0, 1'b0);
  or or_11 (X4, 1'b0, 1'b0);
  or or_12 (X6, T3, T12, 1'b0);
  or or_13 (X8, T2, T4, T6, 1'b0, T9, T11);
  or or_14 (LOAD_AR, T1, T3, T5, T12, T8, T10);
  Demultiplexer #(.select(4)) demultiplexer_1 (
    .out0(T0), .out1(T1), .out2(T2), .out3(T3), .out4(T4), .out5(T5), .out6(T6), .out7(T7), .out8(T8),
    .out9(T9), .out10(T10), .out11(T11), .out12(T12), .out13(T13), .out14(T14), .out15(T15), .in(1'b1),
    .sel(adder_1_out));
  or or_15 (Write_en, T13, 1'b0);
  or or_16 (X7, 1'b0, 1'b0);
  Priority_Encoder priority_encoder_1 (
    .in0(X1), .in1(X2), .in2(X3), .in3(X4), .in4(X5), .in5(X6), .in6(X7), .in7(X8), .out(SELECT_OUT));  // open: en_in, gs, en_out
  or or_17 (CLR_AR, Start, 1'b0, 1'b0);
  or or_18 (LOAD_PC, 1'b0, 1'b0);
  or or_19 (INR_PC, T2, T7, T4, T9);
  or or_20 (CLR_DR, 1'b0, Start);
  or or_21 (LOAD_ALU, T7, T10);
  or or_22 (CLR_AC, Start, 1'b0);
  or or_23 (IR_LDR, T2, T6, T9, T11);
  or or_24 (CLR_TR, 1'b0, Start);
  or or_25 (X1, 1'b0, 1'b0);
  or or_26 (X3, T1, T5, T10, T8);
  or or_27 (X5, T13, 1'b0);
  Decoder #(.select(5)) decoder_1 ();  // open: out0, out1, out2, out3, out4, out5, out6, out7, out8, out9, out10, out11, out12, out13, out14, out15, out16, out17, out18, out19, out20, out21, out22, out23, out24, out25, out26, out27, out28, out29, out30, out31, sel, en
endmodule
